# Fritzing sketch sketch (saved by Fritzing 0.9.3b)
breadboards: 1

parts:
  Button_1 = Pushbutton [package="[THT]"]
  LED_2 = LED - 5mm [color="Red (633nm)" package="5 mm [THT]"]
  Raspberry_Pi_1 = Raspberry Pi 3 [part_number=RPI-3-V1.2]
  LED_1 = LED - 5mm [color="Blue (470nm)" package="5 mm [THT]"]
  R3 = Resistor [tolerance=±5% resistance=100 package=THT]
  Button_2 = Pushbutton [package="[THT]"]
  R2 = Resistor [tolerance=±5% resistance=100 package=THT]

nets:
  N1: Button_1.Pin_1, Button_1.Pin_2, Raspberry_Pi_1.GND, R3.Pin_0, Button_2.Pin_1, Button_2.Pin_2, R2.Pin_0
  N2: Button_1.Pin_3, Button_1.Pin_4, Raspberry_Pi_1.GPIO17
  N3: LED_2.cathode, R2.Pin_1
  N4: LED_2.anode, Raspberry_Pi_1.GPIO22
  N5: Raspberry_Pi_1.GPIO4, LED_1.anode
  N6: Raspberry_Pi_1.GPIO27, Button_2.Pin_3, Button_2.Pin_4
  N7: LED_1.cathode, R3.Pin_1

notes:
  LED 2 (print_led_pin)
  LED 1 (picture_led_pin)
  Button 1 (picture_btn_pin)
  Button 2 (print_btn_pin)
